// Digital circuit CPU_main.dig as structural Verilog
module CPU_main (
);

  wire Acc_in, Acc_out, ALU_out, B_reg_in, CLR_T, IR_in, IR_MAR, IR_out, LDA_instr, MAR_in, MEM_ACC, MEM_out,
       PC_enable, PC_load, PC_out, RESET_CLK, T1, T2, T3, T4, T5, T6;
  wire [0:0] CONTROL_ROM_d;
  wire [2:0] ALU_Op, COUNTER;
  wire [3:0] ADRESS, OPCODE;
  wire [7:0] Acc_q, alu_main_1_p3, PC_out_2, W_BUS;

  CounterPreset PC (.en(PC_enable), .in(W_BUS[0]), .ld(PC_load), .out(PC_out_2[0]));  // open: C, dir, clr, ovf
  assign W_BUS = PC_out ? PC_out_2 : 8'bz;  // Driver driver_1
  ROM #(.AddrBits(7), .Bits(16)) CONTROL_ROM (
    .A({COUNTER, OPCODE}),
    .D({ALU_Op, PC_out, MAR_in, MEM_out, IR_in, IR_out, Acc_in, Acc_out, ALU_out, B_reg_in, PC_enable, PC_load, CLR_T, CONTROL_ROM_d[0]}));  // open: sel
  Counter #(.Bits(3)) u_Counter (.clr(CLR_T), .out(COUNTER));  // open: en, C, ovf
  // Probe on W_BUS
  ROM #(.AddrBits(8), .Bits(8)) ROM (.sel(MEM_out), .D(W_BUS));  // open: A
  Decoder #(.Selector_Bits(3)) decoder_1 (
    .sel(COUNTER), .out_0(T1), .out_1(T2), .out_2(T3), .out_3(T4), .out_4(T5), .out_5(T6));  // open: out_6, out_7
  Register #(.Bits(8)) Acc (.en(Acc_in), .Q(Acc_q));  // open: D, C
  Decoder #(.Selector_Bits(4)) decoder_2 (
    .sel(OPCODE), .out_0(LDA_instr));  // open: out_1, out_2, out_3, out_4, out_5, out_6, out_7, out_8, out_9, out_10, out_11, out_12, out_13, out_14, out_15
  assign W_BUS = Acc_out ? Acc_q : 8'bz;  // Driver driver_2
  Register #(.Bits(8)) IR (.D(W_BUS), .en(IR_in), .Q({ADRESS, OPCODE}));  // open: C
  // ALU_main alu_main_1: pin names not known; wires that end beside it: W_BUS, ALU_Op, alu_main_1_p3
  assign W_BUS = IR_out ? {ADRESS, OPCODE} : 8'bz;  // Driver driver_3
  assign W_BUS = ALU_out ? alu_main_1_p3 : 8'bz;  // Driver driver_4
  Register #(.Bits(8)) B_reg (.D(W_BUS), .en(B_reg_in));  // open: C, Q
  Register #(.Bits(8)) Out_reg (.D(W_BUS));  // open: C, en, Q
  and and_1 (IR_MAR, T4, LDA_instr);
  and and_2 (MEM_ACC, T5, LDA_instr);
  and and_3 (RESET_CLK, T6, LDA_instr);
  Register #(.Bits(8)) MAR (.D(W_BUS), .en(MAR_in));  // open: C, Q
  // Pins of 1 and 8 bits meet at W_BUS
  // Pins of 1 and 8 bits meet at PC_out_2

  // Notes on the sheet:
  //   contents of CONTROL_ROM (hex, n*v repeats v):
  //   1800,8,600,900,480,2
endmodule
